# Fritzing sketch Electrical schematic holonomic platform (saved by Fritzing 0.9.3b)

parts:
  S1 = H-Bridge with L298N
  S2 = H-Bridge with L298N
  DC_Mot_Enc1 = DC Motor with two-phase hall-encoder [part_number=VT-E-G25A-06-177E]
  DC_Mot_Enc4 = DC Motor with two-phase hall-encoder [part_number=VT-E-G25A-06-177E]
  X1 = USB Connectors [package=usb-a-s-nosilk]  # not connected
  Raspberry_Pi_1 = Raspberry Pi 4 [part_number=RPI-4-b]
  X2 = USB Connectors [package=usb-a-s-nosilk]  # not connected
  BAT1 = 6v battery [package=battery]
  DC_Mot_Enc5 = DC Motor with two-phase hall-encoder [part_number=VT-E-G25A-06-177E]
  DC_Mot_Enc6 = DC Motor with two-phase hall-encoder [part_number=VT-E-G25A-06-177E]

nets:
  12V: S1.12V, S2.12V, BAT1.+
  GND: S1.GND, S2.GND, BAT1.-
  5V: S1.5V, S2.5V, Raspberry_Pi_1.5V
  N1: S1.ENA, Raspberry_Pi_1.GPIO18
  N2: S1.IN1, Raspberry_Pi_1.GPIO27
  N3: S1.IN2, Raspberry_Pi_1.GPIO23
  N4: S1.IN3, Raspberry_Pi_1.GPIO22
  N5: S1.IN4, Raspberry_Pi_1.GPIO24
  N6: S1.ENB, Raspberry_Pi_1.GPIO19
  N7: S1.M1-01, DC_Mot_Enc5.pin2
  N8: S1.M1-02, DC_Mot_Enc5.pin1
  N9: S1.M2-01, DC_Mot_Enc6.pin2
  N10: S1.M2-02, DC_Mot_Enc6.pin1
  N11: S2.ENA, Raspberry_Pi_1.GPIO12
  N12: S2.IN1, Raspberry_Pi_1.GPIO10
  N13: S2.IN2, Raspberry_Pi_1.GPIO25
  N14: S2.IN3, Raspberry_Pi_1.GPIO9
  N15: S2.IN4, Raspberry_Pi_1.GPIO8
  N16: S2.ENB, Raspberry_Pi_1.GPIO13
  N17: S2.M1-01, DC_Mot_Enc1.pin2
  N18: S2.M1-02, DC_Mot_Enc1.pin1
  N19: S2.M2-01, DC_Mot_Enc4.pin2
  N20: S2.M2-02, DC_Mot_Enc4.pin1

notes:
  Motor Left front
  Motor right front
  Motor left back
  Motor right back
  MotorShield 1
  MotorShield 2
  2x USB for powering PI's
  2x USB for powering tags
  Raspberry PI 4
  12V Battery

custom parts:
  H-Bridge with L298N: h-bridge
  Raspberry Pi 4: The RPi4, a faster version of the awesome Raspberry Pi 2 B ARM Board with 40 pin gpio. Ready for special Raspberry Pi B+ and RPi2 Hat (Hardware attached (on) top)
  6v battery: 6V lead acid battery 12ah
