# Fritzing sketch colab elec (saved by Fritzing 0.9.3b)

parts:
  Raspberry_Pi_2 = Raspberry Pi 4 [part_number=RPI-4-b]
  U1 = GAS_SENSOR [package=mq-3]
  LED1 = LEDs [package=led10mm]
  LED2 = LEDs [package=led10mm]
  R2 = Resistor [tolerance=±5% resistance=220 package="0402 [SMD]"]
  LED3 = LEDs [package=led10mm]
  R3 = Resistor [tolerance=±5% resistance=220 package="0402 [SMD]"]
  LED4 = LEDs [package=led10mm]
  R4 = Resistor [tolerance=±5% resistance=220 package="0402 [SMD]"]
  LED5 = LEDs [package=led10mm]
  R5 = Resistor [tolerance=±5% resistance=220 package="0402 [SMD]"]
  LED6 = LEDs [package=led10mm]
  R6 = Resistor [tolerance=±5% resistance=220 package="0402 [SMD]"]

nets:
  N1: Raspberry_Pi_2.3v3, LED1.A
  N2: Raspberry_Pi_2.GPIO27, R4.Pin_1
  N3: Raspberry_Pi_2.GPIO25, R6.Pin_1
  N4: Raspberry_Pi_2.GPIO23, R5.Pin_1
  N5: Raspberry_Pi_2.GND, U1.A1, LED1.C, LED2.C, LED3.C, LED4.C, LED5.C, LED6.C
  N6: Raspberry_Pi_2.GPIO18, R3.Pin_1
  N7: Raspberry_Pi_2.GPIO15, R2.Pin_1
  N8: Raspberry_Pi_2.5V, U1.B1
  N9: LED2.A, R2.Pin_0
  N10: LED3.A, R3.Pin_0
  N11: LED4.A, R4.Pin_0
  N12: LED5.A, R5.Pin_0
  N13: LED6.A, R6.Pin_0

custom parts:
  Raspberry Pi 4: The RPi4, a faster version of the awesome Raspberry Pi 2 B ARM Board with 40 pin gpio. Ready for special Raspberry Pi B+ and RPi2 Hat (Hardware attached (on) top)
